# Fritzing sketch assemble (saved by Fritzing 0.9.3b)
circuit board: 10.1363cm x 6.63857cm
breadboards: 2

parts:
  DEC = Pololu A4988 [package=SO16]
  RA = Pololu A4988 [package=SO16]
  12V = Power plug
  IC1 = IC, DIP package, 30 pins [chip_label=ESP32-WROOM]
  5V = Power plug
  Display = Grove OLED 128x96
  Focuser = ULN2003A [package="DIP16 [THT]"]

nets:
  N1: DEC.ENABLE, IC1.pin28
  VDD: DEC.MS1, DEC.MS2, DEC.MS3, DEC.VDD, RA.MS1, RA.MS2, RA.MS3, RA.VDD, IC1.pin30, 5V.VCC
  N2: DEC.RESET, DEC.SLEEP
  N3: DEC.STEP, IC1.pin27
  N4: DEC.DIR, IC1.pin26
  GND: DEC.GND, RA.GND, IC1.pin2
  N5: DEC.VMOT, RA.VMOT, 12V.VCC
  N6: RA.ENABLE, IC1.pin25
  N7: RA.RESET, RA.SLEEP
  N8: RA.STEP, IC1.pin24
  N9: RA.DIR, IC1.pin23
  GND_2: 12V.GND, IC1.pin29, 5V.GND, Display.GND
  N10: IC1.pin1, Display.VCC
  N11: IC1.pin8, Focuser.In_1
  N12: IC1.pin9, Focuser.In_2
  N13: IC1.pin10, Focuser.In_3
  N14: IC1.pin11, Display.SCL
  N15: IC1.pin14, Display.SDA
  N16: IC1.pin15, Focuser.In_4
